// Logisim project cpu.circ as structural Verilog: 1 circuit, main circuit main
module main (
);

  wire and_1_out, and_2_out, and_3_out, and_4_out, clock_1_out, decoder_1_out0, decoder_1_out1,
       decoder_1_out2, decoder_1_out3;
  wire [1:0] multiplexer_1_out;
  wire [7:0] adder_1_out, adder_2_out, multiplexer_2_out, multiplexer_3_out, multiplexer_4_out,
       multiplexer_5_out, multiplexer_6_out, multiplexer_7_out, multiplier_1_out, PC_q, ram_2_dout, X0_q,
       X1_q, X2_q, X3_q;
  wire [15:0] ram_1_dout;

  Clock clock_1 (.out(clock_1_out));
  Register PC (.D(adder_1_out), .en(1'b1), .clk(clock_1_out), .Q(PC_q));  // open: clr
  Adder adder_1 (.a(8'h1), .b(PC_q), .out(adder_1_out), .cin(1'b0));  // open: cout
  RAM #(.dataWidth(16)) ram_1 (.addr(PC_q), .we(1'b0), .oe(1'b1), .clk(clock_1_out), .dout(ram_1_dout));  // open: din
  Multiplexer #(.width(2)) multiplexer_1 (
    .in0(ram_1_dout[9:8]), .in1(ram_1_dout[1:0]), .out(multiplexer_1_out), .sel(ram_1_dout[14]));
  Decoder #(.enable("false"), .select(2)) decoder_1 (
    .out0(decoder_1_out0), .out1(decoder_1_out1), .out2(decoder_1_out2), .out3(decoder_1_out3),
    .sel(ram_1_dout[1:0]));
  and and_1 (and_1_out, decoder_1_out0, ram_1_dout[13]);
  and and_2 (and_2_out, decoder_1_out1, ram_1_dout[13]);
  and and_3 (and_3_out, decoder_1_out2, ram_1_dout[13]);
  and and_4 (and_4_out, decoder_1_out3, ram_1_dout[13]);
  Register X0 (.D(multiplexer_7_out), .en(and_1_out), .clk(clock_1_out), .Q(X0_q));  // open: clr
  Register X1 (.D(multiplexer_7_out), .en(and_2_out), .clk(clock_1_out), .Q(X1_q));  // open: clr
  Register X2 (.D(multiplexer_7_out), .en(and_3_out), .clk(clock_1_out), .Q(X2_q));  // open: clr
  Register X3 (.D(multiplexer_7_out), .en(and_4_out), .clk(clock_1_out), .Q(X3_q));  // open: clr
  Multiplexer #(.select(2), .width(8)) multiplexer_2 (
    .in0(X0_q), .in1(X1_q), .in2(X2_q), .in3(X3_q), .out(multiplexer_2_out), .sel(ram_1_dout[3:2]));
  Multiplexer #(.select(2), .width(8)) multiplexer_3 (
    .in0(X0_q), .in1(X1_q), .in2(X2_q), .in3(X3_q), .out(multiplexer_3_out), .sel(multiplexer_1_out));
  Multiplexer #(.width(8)) multiplexer_4 (
    .in0(multiplexer_3_out), .in1({2'b00, ram_1_dout[9:4]}), .out(multiplexer_4_out), .sel(ram_1_dout[11]));
  Adder adder_2 (.a(multiplexer_2_out), .b(multiplexer_4_out), .out(adder_2_out), .cin(1'b0));  // open: cout
  Multiplier multiplier_1 (
    .a(multiplexer_2_out), .b(multiplexer_4_out), .out(multiplier_1_out), .cin({8{1'b0}}));  // open: cout
  Multiplexer #(.width(8)) multiplexer_5 (
    .in0(adder_2_out), .in1(multiplier_1_out), .out(multiplexer_5_out), .sel(ram_1_dout[12]));
  RAM #(.asyncread("true")) ram_2 (
    .addr(multiplexer_5_out), .we(ram_1_dout[14]), .oe(ram_1_dout[15]), .clk(clock_1_out),
    .din(multiplexer_3_out), .dout(ram_2_dout));
  Multiplexer #(.width(8)) multiplexer_6 (
    .in0(multiplexer_5_out), .in1(ram_2_dout), .out(multiplexer_6_out), .sel(ram_1_dout[15]));
  Multiplexer #(.width(8)) multiplexer_7 (
    .in0(multiplexer_6_out), .in1(multiplexer_4_out), .out(multiplexer_7_out), .sel(ram_1_dout[10]));

  // Notes on the sheet:
  //   Instruction Memory
  //   Control
  //   Reg_1
  //   Reg_d
  //   MOVctrl
  //   Reg_2
  //   ALUop
  //   MemRead
  //   MemWrite
  //   for STR
  //   ALUsrc
  //   WriteReg
  //   immediate
  //   RegWrite
  //   RegDataW
  //   ReadReg2
  //   RegData1
  //   ReadReg1
  //   RegData2
  //   WriteDataM
  //   ALU
  //   Aluout
  //   Data Memory
  //   MemToReg (same as MemRead)
  //   ReadDataM
endmodule
